# Fritzing sketch lixeira-inteligente-completa-conectada (saved by Fritzing 0.9.3b)
breadboards: 1

parts:
  Display = LCD screen
  Controlador_I2C = LCM1602 IIC [part_number="LCM1602 IIC" chip_label="LCM1602 IIC" package="DIP (Dual Inline) [THT]"]
  Sensor_Ultrassonico = hc-sr04
  Componente1 = Arduino Uno (Rev3) - ICSP
  J1 = Basic Servo
  J2 = Basic Servo
  J3 = Basic Servo
  R2 = Resistor [tolerance=±5% resistance=220k package="1206 [SMD]"]
  R3 = Resistor [tolerance=±5% resistance=100k package="1206 [SMD]"]
  R4 = Resistor [tolerance=±5% resistance=1M package="1206 [SMD]"]
  R5 = Resistor [tolerance=±5% resistance=220k package="1206 [SMD]"]
  R6 = Resistor [tolerance=±5% resistance=100k package="1206 [SMD]"]
  R7 = Resistor [tolerance=±5% resistance=1M package="1206 [SMD]"]
  R8 = Resistor [tolerance=±5% resistance=220k package="1206 [SMD]"]
  R9 = Resistor [tolerance=±5% resistance=100k package="1206 [SMD]"]
  D1 = Zener Diode [part_number=1N4732A breakdown_voltage=3.6V package="Melf DO-213 AB [SMD]"]  # not connected
  D2 = Zener Diode [part_number=1N4732A breakdown_voltage=3.6V package="Melf DO-213 AB [SMD]"]
  D3 = Zener Diode [part_number=1N4732A breakdown_voltage=3.6V package="Melf DO-213 AB [SMD]"]
  J4 = Power Jack [package=power_jack_smd]
  U1 = TEMPERATURE-SENSOR [package=to-92]
  U2 = TEMPERATURE-SENSOR [package=to-92]
  U3 = TEMPERATURE-SENSOR [package=to-92]
  R10 = Resistor [tolerance=±5% resistance=1M package="1206 [SMD]"]
  U4 = ESP8266 NodeMCU LoLin module
  R11 = Resistor [tolerance=±5% resistance=220k package="1206 [SMD]"]
  R12 = Resistor [tolerance=±5% resistance=100k package="1206 [SMD]"]  # not connected
  R13 = Resistor [tolerance=±5% resistance=220k package="1206 [SMD]"]  # not connected
  R14 = Resistor [tolerance=±5% resistance=220k package="1206 [SMD]"]  # not connected
  R15 = Resistor [tolerance=±5% resistance=220k package="1206 [SMD]"]

nets:
  N1: Display.V0, Controlador_I2C.V0
  N2: Display.RS, Controlador_I2C.RS
  N3: Display.R/W, Controlador_I2C.RW
  N4: Display.E, Controlador_I2C.E
  N5: Display.DB0, Controlador_I2C.D0
  N6: Display.DB1, Controlador_I2C.D1
  N7: Display.DB2, Controlador_I2C.D2
  N8: Display.DB3, Controlador_I2C.D3
  N9: Display.DB4, Controlador_I2C.D4
  N10: Display.DB5, Controlador_I2C.D5
  N11: Display.DB6, Controlador_I2C.D6
  N12: Display.DB7, Controlador_I2C.D7
  N13: Display.LED+, Controlador_I2C.A
  N14: Display.LED-, Controlador_I2C.K
  GND: Controlador_I2C.GND, Sensor_Ultrassonico.GND, Componente1.GND, J1.gnd, J2.gnd, J3.gnd, D2.anode, D3.anode, J4.GNDBREAK, U1.ADJ, U2.ADJ, U3.ADJ
  N15: Controlador_I2C.VCC, Componente1.A4/SDA
  N16: Controlador_I2C.SDA, Componente1.A5/SCL
  VCC: Controlador_I2C.SCL, Sensor_Ultrassonico.VCC, Componente1.5V, J1.vcc, J2.vcc, J3.vcc
  N17: Controlador_I2C.LED_A, Controlador_I2C.LED_B
  N18: Sensor_Ultrassonico.Trig, Componente1.D2
  N19: Sensor_Ultrassonico.Echo, Componente1.D3_PWM
  N20: Componente1.D8, R10.Pin_0
  N21: Componente1.D9_PWM, R4.Pin_1
  N22: Componente1.D10_PWM/SS, R9.Pin_1
  N23: Componente1.D11_PWM/MOSI, J2.pulse
  N24: Componente1.D12/MISO, J3.pulse
  N25: Componente1.D13/SCK, J1.pulse
  N26: Componente1.D4, R11.Pin_1
  N27: R2.Pin_0, R10.Pin_1
  N28: R2.Pin_1, R3.Pin_1
  N29: R3.Pin_0, U3.VCC
  N30: R4.Pin_0, R5.Pin_0
  N31: R5.Pin_1, R6.Pin_0
  N32: R6.Pin_1, D2.cathode, U2.VCC
  N33: R7.Pin_0, D3.cathode, U1.VCC
  N34: R7.Pin_1, R8.Pin_1, R9.Pin_0
  GND_2: J4.GND, U1.GND, U2.GND, U3.GND
  N35: U4.D1, R15.Pin_1
  N36: R11.Pin_0, R15.Pin_0

custom parts:
  LCM1602 IIC: I2C-Module to use a 1602 or 2004 LCD on with the wire.h libory Serial LCD Modul
  ESP8266 NodeMCU LoLin module: ESP8266 based NodeMCU

// code stored in the sketch: LixeiraInteligente.ino

